# Fritzing sketch jacket (saved by Fritzing 0.9.2b)
breadboards: 1

parts:
  Part1 = Photon
  SENSOR1 = TCS34725 RGB Color Sensor
  U1 = LIPO-2000mAh [package=lipo-2000]
  NEOPIXEL1 = Neopixel Strip -- White (60/m)
  NEOPIXEL2 = Neopixel Strip -- White (60/m)
  NEOPIXEL3 = Neopixel Strip -- White (60/m)
  BATT1 = 4xAA Switchable Battery Pack w/Bare Wire

nets:
  N1: Part1.A0, NEOPIXEL1.+5V
  N2: Part1.A1, NEOPIXEL3.+5V
  GND: Part1.GND, SENSOR1.GND, U1.-, NEOPIXEL1.GND, NEOPIXEL2.GND, NEOPIXEL3.GND, BATT1.NEG
  N3: Part1.VIN, U1.+
  N4: Part1.D0, SENSOR1.SDA
  N5: Part1.D1, SENSOR1.SCL
  N6: Part1.D2, NEOPIXEL2.+5V
  3V3: Part1.3V3, SENSOR1.3V3
  N7: NEOPIXEL1.DI, NEOPIXEL2.DI, NEOPIXEL3.DI, BATT1.POS

notes:
  [Pretend this breadboard is an Internet Button Shield]
  ...you'll also need to de-solder the buzzer. Because it prevents working with the TCS color sensor, as it's an I2C device
  Each of these strips represents a light-up places of the jacket-- left arm square, right arm square, and hood strip.
  Use 4 AA recharageables OR 3 AAs and solder the last battery slot together.

custom parts:
  TCS34725 RGB Color Sensor: TCS34725 RGB Color Sensor with LED
  Neopixel Strip -- White (60/m): Neopixel Strip, White, 60 pixels per meter.
  4xAA Switchable Battery Pack w/Bare Wire: 4xAA Switchable Battery Pack with Bare Wire connection
